# Fritzing sketch unkrautroboter (saved by Fritzing 1.0.5)

parts:
  XL4015 = RioRand LM2596
  D1 = SOLAR-IXYS [package=solarbit-12x1]
  LED1 = RGB LED (com. cathode, rbg) [color="Red (633nm)" current=0.030A package="5 mm [THT]"]
  XL4015_2 = RioRand LM2596
  Bauteil2 = Arduino Pro Mini (5V)
  U2 = LIPO-2000mAh [package=lipo-2000]
  Bauteil3 = Arduino Mega 2560 (Rev3)
  Mod2 = Raspberry Pi 4B
  Hauptsystem = HFD2-012-M-L2 Latching relay [part_number=HFD2-012-M-L2 package="DIP (Dual Inline) [THT]"]
  Bauteil4 = INA 260
  Grove1 = Grove OLED 128x96  # not connected
  6N137_Optokoppler = Optocoupler [package=THT]
  M1 = BTS7960
  M2 = Pololu 37D metal gear motor
  M3 = BTS7960
  M4 = Pololu 37D metal gear motor
  M5 = BTS7960
  M6 = Pololu 37D metal gear motor
  M7 = BTS7960
  M8 = Pololu 37D metal gear motor
  M9 = BTS7960
  M10 = Pololu 37D metal gear motor
  PreCharge = HFD2-012-M-L2 Latching relay [part_number=HFD2-012-M-L2 package="DIP (Dual Inline) [THT]"]
  RY3 = HFD2-012-M-L2 Latching relay [part_number=HFD2-012-M-L2 package="DIP (Dual Inline) [THT]"]
  RY4 = HFD2-012-M-L2 Latching relay [part_number=HFD2-012-M-L2 package="DIP (Dual Inline) [THT]"]
  Mod3 = Solar Charge Controller [part_number="KLD Series Solar Charge Controller PWM" package=PWM-Model]
  R1 = Resistor [tolerance=±5% power=0.25W resistance=220 package=THT]

nets:
  N1: XL4015.Pin_1, U2.+, RY3.pin13
  N2: D1.A, RY4.pin4
  N3: D1.C, Mod3.Connector_2
  N4: LED1.red_anode, Bauteil2.MISO
  N5: LED1.blue_anode, Bauteil2.MOSI
  N6: LED1.green_anode, Bauteil2.D10
  N7: XL4015_2.Pin_1, Hauptsystem.pin8, R1.Pin_1
  N8: Bauteil2.D9, Hauptsystem.pin2
  N9: Bauteil2.D8, Hauptsystem.pin1
  N10: Bauteil2.D7, PreCharge.pin2
  N11: Bauteil2.D6, PreCharge.pin1
  N12: Bauteil2.D5, RY3.pin2
  N13: Bauteil2.D4, RY3.pin1
  N14: Bauteil2.D3, RY4.pin2
  N15: Bauteil2.D2, RY4.pin1
  N16: Bauteil3.D21/SCL, Bauteil3.SCL, Bauteil4.SCL
  N17: Bauteil3.D20/SDA, Bauteil3.SDA, Bauteil4.SDA
  N18: Bauteil3.D19/RX1, Mod2.GPIO15
  N19: Bauteil3.D18/TX1, 6N137_Optokoppler.Pin_1
  N20: Mod2.GPIO14, 6N137_Optokoppler.Pin_6
  N21: M1.pin3, M1.pin4, M1.pin7
  N22: M1.pin9, M2.Pin_6
  N23: M1.pin10, M2.Pin_5
  N24: M3.pin3, M3.pin4, M3.pin7
  N25: M3.pin9, M4.Pin_6
  N26: M3.pin10, M4.Pin_5
  N27: M5.pin3, M5.pin4, M5.pin7
  N28: M5.pin9, M6.Pin_6
  N29: M5.pin10, M6.Pin_5
  N30: M7.pin3, M7.pin4, M7.pin7
  N31: M7.pin9, M8.Pin_6
  N32: M7.pin10, M8.Pin_5
  N33: M9.pin3, M9.pin4, M9.pin7
  N34: M9.pin9, M10.Pin_6
  N35: M9.pin10, M10.Pin_5
  N36: PreCharge.pin8, R1.Pin_0
  N37: PreCharge.pin15, PreCharge.pin16
  N38: RY3.pin9, Mod3.Connector_3
  N39: RY4.pin8, Mod3.Connector_1

notes:
  5V

custom parts:
  HFD2-012-M-L2 Latching relay: Dual coil dpdt latching relay.
  INA 260: Rev. B, add copy
  BTS7960: BTS7960 43A Peak Power H-Bridge PWM Motor Driver
  Pololu 37D metal gear motor: Pololu 37D metal gear motor.
  Solar Charge Controller: PWM-Solar Charge Controller
